// Logisim project zaid.circ as structural Verilog
module main (
  input  in_1,
  input  in_2,
  input  in_3,
  output out_4,
  output out_5,
  output out_6,
  output out_7,
  output out_8,
  output out_9,
  output out_10,
  output out_11,
  output out_12,
  output out_13,
  output out_14,
  output out_15
);

  wire clock_1_out;
  wire [31:0] adder_1_out, register_1_q;
  wire [31:6] rom_1_data;

  Register #(.width(32)) register_1 (.D(adder_1_out), .en(in_1), .Q(register_1_q), .clk(clock_1_out), .clr(in_2));
  Clock clock_1 (.out(clock_1_out));
  // Probe on register_1_q
  Adder #(.width(32)) adder_1 (.a(register_1_q), .b(32'h4), .out(adder_1_out));  // open: cin, cout
  // Probe on {rom_1_data, {6{rom_1_data[6]}}}
  ROM #(.addrWidth(24), .dataWidth(32)) rom_1 (
    .addr(register_1_q[25:2]), .data({rom_1_data, {6{rom_1_data[6]}}}), .sel(in_3));
  decoder decoder_1 ();
endmodule

module opcode (
  input  [6:0] in_1,
  input  [1:0] in_2,
  output add,
  output sub,
  output addi,
  output lui,
  output slli,
  output lw,
  output sw,
  output beq,
  output bne,
  output blt,
  output bge,
  output jal
);

  wire and_1_out, nand_1_out, nand_2_out, nand_3_out, nand_4_out, nand_5_out, nand_6_out, nand_7_out,
       nand_8_out, nand_9_out, nand_10_out, nand_11_out, nand_12_out, nand_13_out, nand_14_out, nand_15_out,
       nand_16_out, nand_17_out, nand_18_out, nand_19_out, nand_20_out, nand_21_out, nand_22_out,
       nand_23_out, nand_24_out, nand_25_out, nand_26_out, nand_27_out, nand_28_out, nand_29_out,
       nand_30_out, nand_31_out, nand_32_out, nand_33_out, nand_34_out, nand_35_out, nand_36_out,
       nand_37_out, nand_38_out, nand_39_out, nand_40_out, nand_41_out, nand_42_out, nand_43_out,
       nand_44_out, nand_45_out, nand_46_out, nand_47_out, nand_48_out, nand_49_out, nand_50_out,
       nand_51_out, nand_52_out;

  nand nand_1 (nand_1_out, in_1[6], in_1[6]);
  nand nand_2 (nand_2_out, in_1[3], in_1[3]);
  nand nand_3 (nand_3_out, in_1[2], in_1[2]);
  nand nand_4 (nand_4_out, in_1[6], in_1[6]);
  nand nand_5 (nand_5_out, in_1[3], in_1[3]);
  nand nand_6 (nand_6_out, in_1[2], in_1[2]);
  nand nand_7 (nand_7_out, in_1[6], in_1[6]);
  nand nand_8 (nand_8_out, in_1[5], in_1[5]);
  nand nand_9 (nand_9_out, in_1[3], in_1[3]);
  nand nand_10 (nand_10_out, in_1[2], in_1[2]);
  nand nand_11 (nand_11_out, in_1[6], in_1[6]);
  nand nand_12 (nand_12_out, in_1[3], in_1[3]);
  nand nand_13 (nand_13_out, in_1[6], in_1[6]);
  nand nand_14 (nand_14_out, in_1[5], in_1[5]);
  nand nand_15 (nand_15_out, in_1[3], in_1[3]);
  nand nand_16 (nand_16_out, in_1[2], in_1[2]);
  nand nand_17 (nand_17_out, in_1[6], in_1[6]);
  nand nand_18 (nand_18_out, in_1[5], in_1[5]);
  nand nand_19 (nand_19_out, in_1[4], in_1[4]);
  nand nand_20 (nand_20_out, in_1[3], in_1[3]);
  nand nand_21 (nand_21_out, in_1[2], in_1[2]);
  nand nand_22 (nand_22_out, in_1[6], in_1[6]);
  nand nand_23 (nand_23_out, in_1[4], in_1[4]);
  nand nand_24 (nand_24_out, in_1[3], in_1[3]);
  nand nand_25 (nand_25_out, in_1[2], in_1[2]);
  nand nand_26 (nand_26_out, in_1[4], in_1[4]);
  nand nand_27 (nand_27_out, in_1[3], in_1[3]);
  nand nand_28 (nand_28_out, in_1[2], in_1[2]);
  nand nand_29 (nand_29_out, in_1[4], in_1[4]);
  nand nand_30 (nand_30_out, in_1[3], in_1[3]);
  nand nand_31 (nand_31_out, in_1[2], in_1[2]);
  nand nand_32 (nand_32_out, in_1[4], in_1[4]);
  nand nand_33 (nand_33_out, in_1[3], in_1[3]);
  nand nand_34 (nand_34_out, in_1[2], in_1[2]);
  nand nand_35 (nand_35_out, in_1[4], in_1[4]);
  nand nand_36 (nand_36_out, in_1[3], in_1[3]);
  nand nand_37 (nand_37_out, in_1[2], in_1[2]);
  nand nand_38 (nand_38_out, in_1[4], in_1[4]);
  nand nand_39 (nand_39_out, nand_1_out, in_1[5], in_1[4], nand_2_out, nand_3_out, in_1[1], in_1[0]);
  nand nand_40 (nand_40_out, nand_4_out, in_1[5], in_1[4], nand_5_out, nand_6_out, in_1[1], in_1[0]);
  nand nand_41 (nand_41_out, nand_7_out, nand_8_out, in_1[4], nand_9_out, nand_10_out, in_1[1], in_1[0]);
  nand nand_42 (nand_42_out, nand_11_out, in_1[5], in_1[4], nand_12_out, in_1[2], in_1[1], in_1[0]);
  nand nand_43 (nand_43_out, nand_13_out, nand_14_out, in_1[4], nand_15_out, nand_16_out, in_1[1], in_1[0]);
  nand nand_44 (nand_44_out, nand_17_out, nand_18_out, nand_19_out, nand_20_out, nand_21_out, in_1[1], in_1[0]);
  nand nand_45 (nand_45_out, nand_22_out, in_1[5], nand_23_out, nand_24_out, nand_25_out, in_1[1], in_1[0]);
  nand nand_46 (nand_46_out, in_1[6], in_1[5], nand_26_out, nand_27_out, nand_28_out, in_1[1], in_1[0]);
  nand nand_47 (nand_47_out, in_1[6], in_1[5], nand_29_out, nand_30_out, nand_31_out, in_1[1], in_1[0]);
  nand nand_48 (nand_48_out, in_1[6], in_1[5], nand_32_out, nand_33_out, nand_34_out, in_1[1], in_1[0]);
  nand nand_49 (nand_49_out, in_1[6], in_1[5], nand_35_out, nand_36_out, nand_37_out, in_1[1], in_1[0]);
  nand nand_50 (nand_50_out, in_1[6], in_1[5], nand_38_out, in_1[3], in_1[2], in_1[1], in_1[0]);
  nand nand_51 (nand_51_out, nand_39_out, nand_39_out);
  nand nand_52 (nand_52_out, nand_40_out, nand_40_out);
  nand nand_53 (addi, nand_41_out, nand_41_out);
  nand nand_54 (lui, nand_42_out, nand_42_out);
  nand nand_55 (slli, nand_43_out, nand_43_out);
  nand nand_56 (lw, nand_44_out, nand_44_out);
  nand nand_57 (sw, nand_45_out, nand_45_out);
  nand nand_58 (beq, nand_46_out, nand_46_out);
  nand nand_59 (bne, nand_47_out, nand_47_out);
  nand nand_60 (blt, nand_48_out, nand_48_out);
  nand nand_61 (bge, nand_49_out, nand_49_out);
  nand nand_62 (jal, nand_50_out, nand_50_out);
  buf and_1 (and_1_out, nand_52_out);  // AND_Gate
  Demultiplexer #(.select(2)) demultiplexer_1 (
    .out0(add), .out2(sub), .in(and_1_out), .sel(in_2));  // open: out1, out3, en
endmodule
